# Fritzing sketch schematic (saved by Fritzing 0.9.4)
breadboards: 1

parts:
  Raspberry_Pi_5_8GB = Raspberry Pi B+
  MCP3008 = MCP3008 [package=dil16]  # not connected
  S1 = Momentary Switch [package=tactile-pth]
  R1 = Resistor [tolerance=±5% resistance=470 package="0805 [SMD]"]
  R2 = Trimmer Potentiometer [maximum_resistance=10kΩ package=THT]
  DS1 = DS18B20 1-Wire Temperature Sensor [part_number=DS18B20]
  R3 = Resistor [tolerance=±5% resistance=4.7k package="0805 [SMD]"]
  R4 = Photocell (LDR) [package=THT]
  R5 = Resistor [tolerance=±5% resistance=10k package="0805 [SMD]"]
  R6 = Resistor [tolerance=±5% resistance=470 package="0805 [SMD]"]
  Reed_switch = SWITCH-MOMENTARY-2 [package=reed_switch_pth]
  IR1 = TSOP312.., 314.. [package=THT]
  D2 = SOLAR-IXYS [package=solarbit-12x1]  # not connected
  Powerbank_5V = BC9VPC [package=bc9vpc]
  INA1 = INA219 DC Current Sensor Breakout
  RFID = RFID-RC522-v2
  LED1 = LEDs [package=led10mm]
  LED2 = LEDs [package=led10mm]
  LED4 = LEDs [package=led10mm]
  LED_3 = LEDs [package=led10mm]
  M1 = DC Motor
  LED5 = LEDs [package=led10mm]
  INA2 = INA219 DC Current Sensor Breakout
  INA3 = INA219 DC Current Sensor Breakout
  INA4 = INA219 DC Current Sensor Breakout
  R7/Heating_pad = Resistor [tolerance=±5% resistance=10 package="2512 [SMD]"]
  Q1 = TRANSISTOR_NPN [package=to-92]
  Q2 = TRANSISTOR_NPN [package=to-92]
  5V_TO_3V3 = Transformer [package=transformer_smd]
  R6_2 = Resistor [tolerance=±5% resistance=470 package="2512 [SMD]"]
  R5_2 = Resistor [tolerance=±5% resistance=470 package="2512 [SMD]"]
  R1_2 = Resistor [tolerance=±5% resistance=100 package="0805 [SMD]"]
  R3_2 = Resistor [tolerance=±5% resistance=100 package="0805 [SMD]"]
  R2_2 = Resistor [tolerance=±5% resistance=100 package="0805 [SMD]"]
  D1 = Rectifier Diode [package="Melf DO-213 AA [SMD]"]
  R8/Heating_pad = Resistor [tolerance=±5% resistance=10 package="2512 [SMD]"]
  R4_2 = Resistor [tolerance=±5% resistance=100 package="0805 [SMD]"]
  Q3 = TRANSISTOR_NPN [package=to-92]
  Q4 = TRANSISTOR_NPN [package=to-92]
  R9 = Resistor [tolerance=±5% resistance=2k package="2512 [SMD]"]
  R10 = Resistor [tolerance=±5% resistance=2k package="2512 [SMD]"]
  Q5 = TRANSISTOR_NPN [package=to-92]
  R11 = Resistor [tolerance=±5% resistance=5.1k package="2512 [SMD]"]

nets:
  N1: Raspberry_Pi_5_8GB.GPIO2, INA1.SDA, INA2.SDA, INA3.SDA, INA4.SDA
  N2: Raspberry_Pi_5_8GB.GPIO3, INA1.SCL, INA2.SCL, INA3.SCL, INA4.SCL
  N3: Raspberry_Pi_5_8GB.GPIO4, DS1.DQ, R3.Pin_1
  N4: Raspberry_Pi_5_8GB.GPIO10, RFID.MOSI
  N5: Raspberry_Pi_5_8GB.GPIO9, RFID.MISO
  N6: Raspberry_Pi_5_8GB.GPIO11, RFID.SCK
  GND: Raspberry_Pi_5_8GB.GND, S1.1, R2.leg2, DS1.GND, R4.pin_0, Reed_switch.1, IR1.GND, Powerbank_5V.V-, INA1.GND, RFID.RST, INA2.GND, INA3.GND, INA4.GND, Q2.E, 5V_TO_3V3.2, 5V_TO_3V3.4
  N7: Raspberry_Pi_5_8GB.GPIO13, IR1.Data
  N8: Raspberry_Pi_5_8GB.GPIO19, R6.Pin_0, Reed_switch.2
  N9: Raspberry_Pi_5_8GB.GPIO26, S1.3, R1.Pin_0
  N10: Raspberry_Pi_5_8GB.GPIO21, R9.Pin_0
  N11: Raspberry_Pi_5_8GB.GPIO20, R10.Pin_0
  N12: Raspberry_Pi_5_8GB.GPIO16, R5_2.Pin_0
  N13: Raspberry_Pi_5_8GB.GPIO12, R6_2.Pin_0
  N14: Raspberry_Pi_5_8GB.GPIO7, RFID.SDA
  N15: Raspberry_Pi_5_8GB.GPIO25, R11.Pin_0
  VCC: R2.leg1, DS1.VDD, R3.Pin_0, R5.Pin_0, R6.Pin_1, INA1.VCC, RFID.3.3V, INA2.VCC, INA3.VCC, INA4.VCC, 5V_TO_3V3.3
  N16: R4.pin_1, R5.Pin_1
  N17: IR1.Vs, Powerbank_5V.V+, INA1.Vin+, LED5.A, INA2.Vin+, INA3.Vin+, INA4.Vin+, 5V_TO_3V3.1
  N18: LED1.C, R1_2.Pin_0
  N19: LED1.A, LED2.A
  N20: LED2.C, R2_2.Pin_0
  N21: LED4.C, R3_2.Pin_0
  N22: LED4.A, LED_3.A, INA2.Vin-
  N23: LED_3.C, R4_2.Pin_0
  N24: M1.pin_1, INA3.Vin-, D1.cathode
  N25: M1.pin_2, Q1.C, D1.anode
  N26: LED5.C, Q5.C
  N27: INA4.Vin-, R7/Heating_pad.Pin_0, R8/Heating_pad.Pin_0
  N28: R7/Heating_pad.Pin_1, Q2.C, R8/Heating_pad.Pin_1
  N29: Q1.E, Q3.E, Q4.E, Q5.E
  N30: Q1.B, R5_2.Pin_1
  N31: Q2.B, R6_2.Pin_1
  N32: R1_2.Pin_1, R2_2.Pin_1, Q4.C
  N33: R3_2.Pin_1, R4_2.Pin_1, Q3.C
  N34: Q3.B, R10.Pin_1
  N35: Q4.B, R9.Pin_1
  N36: Q5.B, R11.Pin_1

custom parts:
  INA219 DC Current Sensor Breakout: INA DC Current Sensor Breakout
  RFID-RC522-v2: A simple China made RFID-RC522 Reader; do check the pin labels, as this is a MFRC522 based clone.
